# Fritzing sketch Fire Alarm (saved by Fritzing 0.9.3b)

parts:
  Flame_Sensor = Keyes IR Infrared Sensor Switch Module
  RELAY = Keyes Relay [package=THT]
  U2 = NodeMCU V1.0
  J1 = Basic Servo
  WATER_PUMP1 = water pump/motor

nets:
  GND: Flame_Sensor.GND, RELAY.ground, U2.GND, J1.gnd, WATER_PUMP1.pin_1
  VCC: Flame_Sensor.VCC, RELAY.power, U2.3V3, J1.vcc
  N1: Flame_Sensor.out, U2.D2
  N2: RELAY.signal, U2.D8
  N3: RELAY.C, U2.Vin
  N4: RELAY.NO, WATER_PUMP1.pin_2
  N5: U2.D4, J1.pulse

custom parts:
  Keyes IR Infrared Sensor Switch Module: An infrared obstacle detector
  Keyes Relay: The Keyes 5V relay module is suitable for SCM development, home appliance control. It uses a 5V~12V TIL control signal which can control DC / AC signal.
  NodeMCU V1.0: ESP8266 based NodeMCU
  water pump/motor: WATER PUMP BY ARDUBLOCKTR
